// Digital circuit tom-1.dig as structural Verilog
module tom_1 (
  input  clk,
  input  in_2,
  output clk_2,
  output clk_not
);

  wire and_1_out, decoder_1_out_0, decoder_1_out_1, decoder_1_out_2, decoder_1_out_3, delay_1_out,
       driver_1_out, nand_1_out, nand_2_out, not_1_out, not_2_out, not_3_out, not_4_out, not_5_out,
       not_6_out, not_8_out, nTOS_eq__eq_0_nis0, PC__LO_ntc, reset_1_out, reset_2_out, TOS__LO_p3;
  wire [7:0] D_i_o, ROM_BUFFER_p4, ROM_d, TOS__HI_p4, TOS__LO_p2, TOS__LO_p4;
  wire [15:0] PC__HI_q, T2SB__HI_p4, TOS__HI_p1;

  assign driver_1_out = in_2 ? clk_not : 1'bz;  // Driver driver_1
  Break break_1 (.brk(driver_1_out));
  tom_1_is0 nTOS_eq__eq_0 (.\input ({TOS__HI_p4, TOS__LO_p4}), .nis0(nTOS_eq__eq_0_nis0));
  SixteenSeg sixteenseg_1 (.led({TOS__HI_p4, TOS__LO_p4}), .dp(1'b0));
  not not_1 (not_1_out, nTOS_eq__eq_0_nis0);
  nand nand_1 (nand_1_out, not_1_out, TOS__LO_p2[7]);
  Delay delay_1 (.in(nand_1_out), .out(delay_1_out));
  Decoder #(.Selector_Bits(2)) decoder_1 (
    .sel(TOS__LO_p2[6:5]), .out_0(decoder_1_out_0), .out_1(decoder_1_out_1), .out_2(decoder_1_out_2),
    .out_3(decoder_1_out_3));
  and and_1 (and_1_out, TOS__LO_p2[3], clk_2);
  not not_2 (not_2_out, decoder_1_out_1);
  not not_3 (not_3_out, decoder_1_out_0);
  not not_4 (not_4_out, TOS__LO_p2[2]);
  not not_5 (not_5_out, TOS__LO_p2[1]);
  not not_6 (not_6_out, TOS__LO_p2[4]);
  tom_269 PC__LO (
    .nPE(delay_1_out), .U_nD(1'b1), .CP(clk_not), .nCEP(1'b0), .nCET(1'b0), .D(ROM_d), .Q(PC__HI_q[7:0]),
    .nTC(PC__LO_ntc));
  tom_269 PC__HI (
    .nPE(delay_1_out), .U_nD(1'b1), .CP(clk_not), .nCEP(PC__LO_ntc), .nCET(1'b0), .D(ROM_BUFFER_p4),
    .Q(PC__HI_q[15:8]));  // open: nTC
  tom_779 D (
    .nOE(TOS__LO_p2[1]), .nCET(TOS__LO_p2[1]), .CP(and_1_out), .S0(not_4_out), .S1(TOS__LO_p2[2]), .I_O(D_i_o));  // open: nTC
  tom_779 R (
    .nOE(not_5_out), .nCET(not_5_out), .CP(and_1_out), .S0(not_4_out), .S1(TOS__LO_p2[2]), .I_O(D_i_o));  // open: nTC
  // tom_374 TOS__LO: pin names not known; wires that end beside it: TOS__HI_p1[7:0], TOS__LO_p2[0], TOS__LO_p3, TOS__LO_p4
  // tom_374 TOS__HI: pin names not known; wires that end beside it: TOS__HI_p1[15:8], TOS__LO_p2[0], TOS__LO_p3, TOS__HI_p4
  Reset reset_1 (.out(reset_1_out));
  not not_7 (TOS__LO_p3, PC__HI_q[0]);
  EEPROM #(.AddrBits(16), .isProgramMemory("true"), .Bits(16)) ROM (
    .A(PC__HI_q), .CS(1'b1), .WE(1'b0), .OE(reset_1_out), .D({TOS__LO_p2, ROM_d}));
  nand nand_2 (nand_2_out, not_2_out, TOS__LO_p2[4]);
  // tom_1_373 T2SB__LO: pin names not known; wires that end beside it: TOS__LO_p4, nand_2_out, 1'b1, T2SB__HI_p4[7:0]
  // tom_1_373 T2SB__HI: pin names not known; wires that end beside it: TOS__HI_p4, nand_2_out, 1'b1, T2SB__HI_p4[15:8]
  RAMSinglePortSel #(.AddrBits(16), .Bits(16)) RAM (
    .A({TOS__HI_p4, TOS__LO_p4}), .CS(~not_2_out), .WE(~TOS__LO_p2[4]), .OE(~not_6_out), .D(T2SB__HI_p4));
  RAMSinglePortSel #(.AddrBits(9), .Bits(16)) STACK (
    .A({TOS__LO_p2[1], D_i_o}), .CS(~1'b0), .WE(~not_6_out), .OE(~TOS__LO_p2[4]), .D(T2SB__HI_p4));
  // tom_374 ROM_BUFFER: pin names not known; wires that end beside it: ROM_d, 1'b0, PC__HI_q[0], ROM_BUFFER_p4
  // tom_1_373 R2TB__LO: pin names not known; wires that end beside it: ROM_d, not_3_out, 1'b1, TOS__HI_p1[7:0]
  // tom_1_373 R2TB__HI: pin names not known; wires that end beside it: ROM_BUFFER_p4, not_3_out, 1'b1, TOS__HI_p1[15:8]
  // tom_1_add ADD: pin names not known; wires that end beside it: {TOS__HI_p4, TOS__LO_p4}, T2SB__HI_p4, decoder_1_out_2, TOS__HI_p1
  tom_1_nand NAND_3 (.A({TOS__HI_p4, TOS__LO_p4}), .B(T2SB__HI_p4), .Vin(decoder_1_out_3), .out(TOS__HI_p1));
  Reset #(.invertOutput("false")) reset_2 (.out(reset_2_out));
  not not_8 (not_8_out, clk);
  assign clk_not = ~reset_2_out ? not_8_out : 1'bz;  // DriverInvSel driverinvsel_1
  assign clk_2 = ~reset_2_out ? clk : 1'bz;  // DriverInvSel driverinvsel_2
  LED led_1 (.in(TOS__LO_p2[0]));
  LED led_2 (.in(TOS__LO_p2[1]));
  LED led_3 (.in(TOS__LO_p2[2]));
  LED led_4 (.in(TOS__LO_p2[3]));
  LED led_5 (.in(TOS__LO_p2[4]));
  LED led_6 (.in(TOS__LO_p2[5]));
  LED led_7 (.in(TOS__LO_p2[6]));
  LED led_8 (.in(TOS__LO_p2[7]));
  // Probe PC on PC__HI_q
  // Probe ROM on {ROM_BUFFER_p4, ROM_d}
  // Probe CTRL on TOS__LO_p2
  // Probe tos_bus on TOS__HI_p1
  // Probe TOS on {TOS__HI_p4, TOS__LO_p4}
  // Probe dr on D_i_o
  // Probe dr_cck on and_1_out
  // Probe stack addr on {TOS__LO_p2[1], D_i_o}
  // Probe stack_bus on T2SB__HI_p4

  // Other names for the same wires on the sheet: clk_t = clk_2; nclk = clk_not

  // Notes on the sheet:
  //   clk: Hz: 3
  //   in_2: default 1
  //   Program
  //   Process
  //   CTRL
  //   TOMSCII
  //   STAGE (PC BIT 0)
  //   contents of ROM (hex, n*v repeats v):
  //   0,100,1c00,1401,1c00,1401,800,4000,1cff,14ff,1e00,4900,1c01,1400,2800,4100,1c01,1400,
  //   3c00,4900,1c01,1400,3c00,4900,1c00,4b00,800,4100,1c00,140a,1cff,14ff,1e00,4900,1cff,
  //   14ff,1e00,4900,1cff,14ff,1e00,4900,1cff,14ff,1e00,4900,1cff,14fe,800,6000,1c00,4b00,
  //   800,4100,1c00,1401,800,4000,1c00,4b00,800,4100,800,4000,1c00,4b00,800,4100,1cff,14ff,
  //   1e00,4900,800,8050,1c00,1400,1c00,1400,800,8052,1cff,14fe,1c00,4b00,800,4100,1c00,
  //   4b00,800,4100,800,8004,1c00,1400,800,8002
  //   0 = TOS-DISABLE
  //   1 = DR-SEL
  //   2 = DR-UP
  //   3 = DR-CCK
  //   4 = STACK-WRITE
  //   5 = TOS-BUS-SEL-1
  //   6 = TOS-BUS-SEL-2
  //   7 = JUMPIF0
endmodule
